# Fritzing sketch sensonation-v2 (saved by Fritzing 0.9.3b)
breadboards: 1

parts:
  Raspberry_Pi1 = Raspberry Pi B rev2
  S1 = SWITCH-MOMENTARY-2 [package=reed_switch_pth]
  S2 = SWITCH-MOMENTARY-2 [package=reed_switch_pth]
  S13 = SWITCH-MOMENTARY-2 [package=reed_switch_pth]
  S14 = SWITCH-MOMENTARY-2 [package=reed_switch_pth]
  S15 = SWITCH-MOMENTARY-2 [package=reed_switch_pth]
  S16 = SWITCH-MOMENTARY-2 [package=reed_switch_pth]
  S17 = SWITCH-MOMENTARY-2 [package=reed_switch_pth]
  S18 = SWITCH-MOMENTARY-2 [package=reed_switch_pth]
  S19 = SWITCH-MOMENTARY-2 [package=reed_switch_pth]
  S20 = SWITCH-MOMENTARY-2 [package=reed_switch_pth]
  M2 = DC Motor
  M1 = DC Motor
  M5 = DC Motor
  M4 = DC Motor
  M3 = DC Motor
  Expander2 = MCP23017 I2C I/O Expander
  Expander1 = MCP23017 I2C I/O Expander
  Controller1 = DRV8833
  Controller2 = DRV8833
  Controller3 = DRV8833
  Controller4 = DRV8833
  Power_plug1 = Power plug

nets:
  VDD: Raspberry_Pi1.5V, Expander2.VDD, Expander2.A2, Expander2.RESET, Expander1.VDD, Expander1.RESET
  N1: Raspberry_Pi1.GPIO_2, Expander2.SDA, Expander1.SDA
  N2: Raspberry_Pi1.GPIO_3, Expander2.SCL, Expander1.SCL
  VSS: Raspberry_Pi1.GND, S1.2, S2.2, S13.2, S14.2, S15.2, S16.2, S17.2, S18.2, S19.2, S20.2, Expander2.VSS, Expander2.A0, Expander2.A1, Expander1.VSS, Expander1.A0, Expander1.A1, Expander1.A2, Controller1.GND#0, Controller2.GND#0, Controller3.GND#0, Controller4.GND#0
  N3: S1.1, Expander1.GPA7
  N4: S2.1, Expander1.GPA6
  N5: S13.1, Expander1.GPA3
  N6: S14.1, Expander1.GPA4
  N7: S15.1, Expander1.GPA2
  N8: S16.1, Expander1.GPA5
  N9: S17.1, Expander2.GPA7
  N10: S18.1, Expander1.GPA0
  N11: S19.1, Expander2.GPA6
  N12: S20.1, Expander1.GPA1
  N13: M2.pin_1, Controller1.AOUT2
  N14: M2.pin_2, Controller1.AOUT1
  N15: M1.pin_1, Controller1.BOUT1
  N16: M1.pin_2, Controller1.BOUT2
  N17: M5.pin_1, Controller3.BOUT1
  N18: M5.pin_2, Controller3.BOUT2
  N19: M4.pin_1, Controller2.AOUT2
  N20: M4.pin_2, Controller2.AOUT1
  N21: M3.pin_1, Controller2.BOUT1
  N22: M3.pin_2, Controller2.BOUT2
  N23: Expander2.GPB0, Controller3.BIN1
  N24: Expander2.GPB1, Controller3.BIN2
  N25: Expander2.GPB2, Controller3.AIN2
  N26: Expander2.GPB3, Controller3.AIN1
  N27: Expander2.GPB4, Controller4.BIN1
  N28: Expander2.GPB5, Controller4.BIN2
  N29: Expander2.GPB6, Controller4.AIN2
  N30: Expander2.GPB7, Controller4.AIN1
  N31: Expander1.GPB0, Controller1.BIN1
  N32: Expander1.GPB1, Controller1.BIN2
  N33: Expander1.GPB2, Controller1.AIN2
  N34: Expander1.GPB3, Controller1.AIN1
  N35: Expander1.GPB4, Controller2.BIN1
  N36: Expander1.GPB5, Controller2.BIN2
  N37: Expander1.GPB6, Controller2.AIN2
  N38: Expander1.GPB7, Controller2.AIN1
  N39: Controller1.GND#8, Controller2.GND#8, Controller3.GND#8, Controller4.GND#8, Power_plug1.GND
  VIN: Controller1.VIN, Controller2.VIN, Controller3.VIN, Controller4.VIN, Power_plug1.VCC

custom parts:
  MCP23017 I2C I/O Expander: The MCP23017 uses two i2c pins (these can be shared with other i2c devices), and in exchange gives you 16 general purpose pins. You can set each of 16 pins to be input, output, input with a pullup or open drain. There's even the ability to get an interrupt via an external pin when any of the inputs change so you don't have to keep polling the chip.
  DRV8833: The DRV8833 provides a dual bridge motor driver solution for toys, printers, and other mechatronic applications.
